// Logisim project addfixed.circ as structural Verilog: 1 circuit, main circuit main
module main (
  input  [7:0] in_1,
  input  [7:0] in_2,
  input  in_3,
  input  Ci,
  input  [31:0] A,
  input  A_2,
  input  B,
  input  Cin,
  input  [31:0] B_2,
  output [7:0] out_10,
  output [31:0] S,
  output Co,
  output [31:0] S_2,
  output Co_2,
  output Sum,
  output Cout
);

  wire adder_2_cout, adder_3_cout, adder_4_cout, adder_5_cout, adder_6_cout, adder_7_cout, and_1_out,
       and_2_out, and_3_out, and_4_out, and_5_out, and_6_out, and_7_out, not_1_out, not_2_out, not_3_out;

  Adder #(.width(32)) adder_1 (.a(A), .b(B_2), .out(S), .cin(Ci), .cout(Co));
  not not_1 (not_1_out, A_2);
  not not_2 (not_2_out, B);
  not not_3 (not_3_out, Cin);
  and and_1 (and_1_out, A_2, not_2_out, not_3_out);
  and and_2 (and_2_out, B, not_1_out, not_3_out);
  and and_3 (and_3_out, Cin, not_2_out, not_1_out);
  and and_4 (and_4_out, Cin, B, A_2);
  and and_5 (and_5_out, A_2, B);
  and and_6 (and_6_out, A_2, Cin);
  and and_7 (and_7_out, B, Cin);
  or or_1 (Cout, and_5_out, and_6_out, and_7_out);
  or or_2 (Sum, and_1_out, and_2_out, and_3_out, and_4_out);
  Adder #(.width(1)) adder_2 (.a(in_1[0]), .b(in_2[0]), .out(out_10[0]), .cin(in_3), .cout(adder_2_cout));
  Adder #(.width(1)) adder_3 (.a(in_1[1]), .b(in_2[1]), .out(out_10[1]), .cin(adder_2_cout), .cout(adder_3_cout));
  Adder #(.width(1)) adder_4 (.a(in_1[2]), .b(in_2[2]), .out(out_10[2]), .cin(adder_3_cout), .cout(adder_4_cout));
  Adder #(.width(1)) adder_5 (.a(in_1[3]), .b(in_2[3]), .out(out_10[3]), .cin(adder_4_cout), .cout(adder_5_cout));
  Adder #(.width(1)) adder_6 (.a(in_1[4]), .b(in_2[4]), .out(out_10[4]), .cin(adder_5_cout), .cout(adder_6_cout));
  Adder #(.width(1)) adder_7 (.a(in_1[5]), .b(in_2[5]), .out(out_10[5]), .cin(adder_6_cout), .cout(adder_7_cout));
  Adder #(.width(1)) adder_8 (.cin(adder_7_cout));  // open: a, b, out, cout

  // Notes on the sheet:
  //   October 4th 2017
  //   One bit adder
endmodule
