// Logisim project shifter8x4BrighentiC.circ as structural Verilog: 2 circuits, main circuit main
module main (
  input  [7:0] in_1,
  input  in_2,
  input  in_3,
  input  in_4,
  input  [1:0] in_5,
  output [7:0] out_6
);

  Multiplexer #(.select(2), .width(8), .enable("false")) multiplexer_1 (
    .in0(in_1), .in1({in_1[6:0], in_2}), .in2({in_1[5:0], {2{in_3}}}), .in3({in_1[4:0], {3{in_4}}}),
    .out(out_6), .sel(in_5));
endmodule

module shifter8x4 (
  input  [7:0] Input,
  input  [1:0] Control,
  output [7:0] Output
);
endmodule
