// Logisim project CPUComponents.circ as structural Verilog: 8 circuits, main circuit ALU
module InstructionDecode (
  input  [31:0] Instruction,
  output [10:0] opcode,
  output [4:0] rn,
  output [4:0] rm,
  output [4:0] rd_rt,
  output [5:0] shamt,
  output [31:0] Sign_Ext_0_31,
  output [10:0] opcodeALU
);


  assign opcode = Instruction[31:21];
  assign opcodeALU = Instruction[31:21];
  assign rd_rt = Instruction[4:0];
  assign rm = Instruction[20:16];
  assign rn = Instruction[9:5];
  assign shamt = Instruction[15:10];
  assign Sign_Ext_0_31 = Instruction;

  // Notes on the sheet:
  //   R-type
endmodule

module Registers (
  input  Write,
  input  [4:0] ReadRegister1,
  input  [4:0] ReadRegister2,
  input  [4:0] WriteRegister,
  input  [31:0] WriteData,
  input  Clear,
  input  Clock,
  output [31:0] ReadData1,
  output [31:0] ReadData2
);

  wire and_1_out, demultiplexer_1_out0, demultiplexer_1_out1, demultiplexer_1_out2, demultiplexer_1_out3,
       demultiplexer_1_out4, demultiplexer_1_out5, demultiplexer_1_out6, demultiplexer_1_out7, not_1_out;
  wire [31:0] registers4_1_readdata1, registers4_1_readdata2, registers4_2_readdata1, registers4_2_readdata2,
       registers4_3_readdata1, registers4_3_readdata2, registers4_4_readdata1, registers4_4_readdata2,
       registers4_5_readdata1, registers4_5_readdata2, registers4_6_readdata1, registers4_6_readdata2,
       registers4_7_readdata1, registers4_7_readdata2, registers4z_1_readdata1, registers4z_1_readdata2;

  Demultiplexer #(.select(3), .enable("false")) demultiplexer_1 (
    .out0(demultiplexer_1_out0), .out1(demultiplexer_1_out1), .out2(demultiplexer_1_out2),
    .out3(demultiplexer_1_out3), .out4(demultiplexer_1_out4), .out5(demultiplexer_1_out5),
    .out6(demultiplexer_1_out6), .out7(demultiplexer_1_out7), .in(and_1_out), .sel(WriteRegister[4:2]));
  and and_1 (and_1_out, Write, not_1_out);
  not not_1 (not_1_out, Clock);
  Registers4 registers4_1 (
    .ReadRegister1(ReadRegister1[1:0]), .ReadRegister2(ReadRegister2[1:0]),
    .WriteRegister(WriteRegister[1:0]), .WriteData(WriteData), .Write(demultiplexer_1_out0), .Clear(Clear),
    .ReadData1(registers4_1_readdata1), .ReadData2(registers4_1_readdata2));
  Registers4 registers4_2 (
    .ReadRegister1(ReadRegister1[1:0]), .ReadRegister2(ReadRegister2[1:0]),
    .WriteRegister(WriteRegister[1:0]), .WriteData(WriteData), .Write(demultiplexer_1_out1), .Clear(Clear),
    .ReadData1(registers4_2_readdata1), .ReadData2(registers4_2_readdata2));
  Registers4 registers4_3 (
    .ReadRegister1(ReadRegister1[1:0]), .ReadRegister2(ReadRegister2[1:0]),
    .WriteRegister(WriteRegister[1:0]), .WriteData(WriteData), .Write(demultiplexer_1_out2), .Clear(Clear),
    .ReadData1(registers4_3_readdata1), .ReadData2(registers4_3_readdata2));
  Registers4 registers4_4 (
    .ReadRegister1(ReadRegister1[1:0]), .ReadRegister2(ReadRegister2[1:0]),
    .WriteRegister(WriteRegister[1:0]), .WriteData(WriteData), .Write(demultiplexer_1_out3), .Clear(Clear),
    .ReadData1(registers4_4_readdata1), .ReadData2(registers4_4_readdata2));
  Registers4 registers4_5 (
    .ReadRegister1(ReadRegister1[1:0]), .ReadRegister2(ReadRegister2[1:0]),
    .WriteRegister(WriteRegister[1:0]), .WriteData(WriteData), .Write(demultiplexer_1_out4), .Clear(Clear),
    .ReadData1(registers4_5_readdata1), .ReadData2(registers4_5_readdata2));
  Registers4 registers4_6 (
    .ReadRegister1(ReadRegister1[1:0]), .ReadRegister2(ReadRegister2[1:0]),
    .WriteRegister(WriteRegister[1:0]), .WriteData(WriteData), .Write(demultiplexer_1_out5), .Clear(Clear),
    .ReadData1(registers4_6_readdata1), .ReadData2(registers4_6_readdata2));
  Registers4 registers4_7 (
    .ReadRegister1(ReadRegister1[1:0]), .ReadRegister2(ReadRegister2[1:0]),
    .WriteRegister(WriteRegister[1:0]), .WriteData(WriteData), .Write(demultiplexer_1_out6), .Clear(Clear),
    .ReadData1(registers4_7_readdata1), .ReadData2(registers4_7_readdata2));
  Registers4Z registers4z_1 (
    .ReadRegister1(ReadRegister1[1:0]), .ReadRegister2(ReadRegister2[1:0]),
    .WriteRegister(WriteRegister[1:0]), .WriteData(WriteData), .Write(demultiplexer_1_out7), .Clear(Clear),
    .ReadData1(registers4z_1_readdata1), .ReadData2(registers4z_1_readdata2));
  Multiplexer #(.select(3), .width(32), .enable("false")) multiplexer_1 (
    .in0(registers4_1_readdata1), .in1(registers4_2_readdata1), .in2(registers4_3_readdata1),
    .in3(registers4_4_readdata1), .in4(registers4_5_readdata1), .in5(registers4_6_readdata1),
    .in6(registers4_7_readdata1), .in7(registers4z_1_readdata1), .out(ReadData1), .sel(ReadRegister1[4:2]));
  Multiplexer #(.select(3), .width(32), .enable("false")) multiplexer_2 (
    .in0(registers4_1_readdata2), .in1(registers4_2_readdata2), .in2(registers4_3_readdata2),
    .in3(registers4_4_readdata2), .in4(registers4_5_readdata2), .in5(registers4_6_readdata2),
    .in6(registers4_7_readdata2), .in7(registers4z_1_readdata2), .out(ReadData2), .sel(ReadRegister2[4:2]));
endmodule

module SignExtend (
  input  [31:0] _0_31,
  output [31:0] out_2
);

  Multiplexer #(.select(2), .width(32), .enable("false")) multiplexer_1 (
    .in1({{7{_0_31[25]}}, _0_31[24:0]}), .in2({{24{_0_31[20]}}, _0_31[19:12]}),
    .in3({{14{_0_31[23]}}, _0_31[22:5]}), .out(out_2), .sel({_0_31[31], _0_31[26]}));  // open: in0
endmodule

module ALU (
  input  [31:0] A,
  input  [31:0] B,
  input  [3:0] Operation,
  output Zero,
  output [31:0] Result,
  output Sign,
  output Overflow,
  output Carry_Out
);

  wire getsign_1_sign, getsign_2_sign;
  wire [31:0] adder_1_out, and_1_out, getsign_1_out_2, getsign_2_out_2, getsign_3_out_2, multiplexer_1_out,
       multiplexer_2_out, not_1_out, not_2_out, or_1_out;

  assign not_1_out = ~A;  // NOT_Gate not_1, 32 bits wide
  assign not_2_out = ~B;  // NOT_Gate not_2, 32 bits wide
  Multiplexer #(.width(32), .enable("false")) multiplexer_1 (
    .in0(A), .in1(not_1_out), .out(multiplexer_1_out), .sel(Operation[3]));
  Multiplexer #(.width(32), .enable("false")) multiplexer_2 (
    .in0(B), .in1(not_2_out), .out(multiplexer_2_out), .sel(Operation[2]));
  GetSign getsign_1 (.in_1(multiplexer_1_out), .Sign(getsign_1_sign), .out_2(getsign_1_out_2));
  GetSign getsign_2 (.in_1(multiplexer_2_out), .Sign(getsign_2_sign), .out_2(getsign_2_out_2));
  Overflow overflow_1 (
    .A(getsign_1_sign), .B(getsign_2_sign), .Result(Sign), .Operation(Operation[1:0]), .Overflow(Overflow));
  assign and_1_out = getsign_1_out_2 & getsign_2_out_2;  // AND_Gate and_1, 32 bits wide
  assign or_1_out = getsign_1_out_2 | getsign_2_out_2;  // OR_Gate or_1, 32 bits wide
  GetSign getsign_3 (.in_1(adder_1_out), .Sign(Sign), .out_2(getsign_3_out_2));
  Adder #(.width(32)) adder_1 (
    .a(getsign_1_out_2), .b(getsign_2_out_2), .out(adder_1_out), .cin(Operation[2]), .cout(Carry_Out));
  Multiplexer #(.select(2), .width(32), .enable("false")) multiplexer_3 (
    .in0(and_1_out), .in1(or_1_out), .in2(getsign_3_out_2), .in3(B), .out(Result), .sel(Operation[1:0]));
  Zero zero_1 (.in_1(Result), .out_2(Zero));

  // Notes on the sheet:
  //   +/-
  //   +/-
  //   +/-
  //   0?
endmodule

module BranchAddress (
  input  [31:0] PC_4,
  input  in_2,
  input  [31:0] Address,
  output [31:0] BranchAddress
);

  Adder #(.width(32)) adder_1 (.a(PC_4), .b({Address[29:0], {2{in_2}}}), .out(BranchAddress));  // open: cin, cout
endmodule

// I-Mem
module Inst_Mem_Interface (
  input  [31:0] Instruction_Address,
  input  [31:0] Mem_To_Interface,
  output [31:0] Instruction,
  output [7:0] To_Inst_Mem
);

  WordAddress wordaddress_1 (.ByteAddress(Instruction_Address), .WordAddress(To_Inst_Mem));  // open: Unaligned

  assign Instruction = Mem_To_Interface;
endmodule

// D Mem
module Data_Mem_Interface (
  input  MemWrite,
  input  MemRead,
  input  [31:0] Data_Address,
  input  [31:0] Data_to_Memory,
  input  [31:0] Data_To_Mem,
  input  Clock___Rising_Edge,
  output [31:0] Data_from_Memory,
  output [7:0] Address_To_Mem,
  output [31:0] Data_From_Mem,
  output [1:0] Mem_Control
);

  wire not_1_out;

  not not_1 (not_1_out, Clock___Rising_Edge);
  WordAddress wordaddress_1 (.ByteAddress(Data_Address), .WordAddress(Address_To_Mem));  // open: Unaligned
  and and_1 (Mem_Control[0], not_1_out, MemWrite);
  MemoryData memorydata_1 (
    .WriteData(Data_to_Memory), .FromMemory(Data_To_Mem), .Write(MemWrite), .Read(MemRead),
    .ReadData(Data_from_Memory), .ToMemory(Data_From_Mem));

  assign Mem_Control[1] = MemRead;
endmodule

module BranchControl (
  input  UnconditionalBranch,
  input  ConditionalBranch__CBZ,
  input  Zero,
  output control
);

  wire and_1_out;

  and and_1 (and_1_out, ConditionalBranch__CBZ, Zero);
  or or_1 (control, UnconditionalBranch, and_1_out);
endmodule
