// Logisim project PipelineARM-CPU1.circ as structural Verilog: 1 circuit, main circuit Datapath
module Datapath (
  input  Reset,
  input  Clear_Instr_Mem,
  input  Clear_Data_Mem
);

  wire ALU_zero, branchcontrol_1_control, Clock_out, Control_alusrc, Control_conditional_branch,
       Control_memread, Control_memtoreg, Control_memwrite, Control_reg2loc, Control_regwrite,
       Control_unconditional_branch, pipereg3ctrl_1_cond_branch_out, pipereg3ctrl_1_memread_out,
       pipereg3ctrl_1_memtoreg_out, pipereg3ctrl_1_memwrite_2, pipereg3ctrl_1_regwrite_out,
       pipereg3ctrl_1_uncond_branch_out, pipereg3dp_1_alu_zero_out, pipereg4crtl_1_memtoreg_out,
       pipereg4crtl_1_regwrite_out, PR2Ctr_alusrc_out, PR2Ctr_cond_branch_out, PR2Ctr_memread_out,
       PR2Ctr_memtoreg_out, PR2Ctr_memwrite_2, PR2Ctr_regwrite_out, PR2Ctr_uncond_branch_out;
  wire [1:0] Control_aluop, data_mem_interface_1_mem_control, PR2Ctr_aluop_out;
  wire [3:0] ALU_Control_operation;
  wire [4:0] instructiondecode_1_rd_rt, instructiondecode_1_rm, instructiondecode_1_rn, multiplexer_1_out,
       pipereg3_4reg_1_destination_reg_2, pipereg3_4reg_2_destination_reg_2, PR2ALUCt_Rt_rt_out;
  wire [7:0] data_mem_interface_1_address_to_mem, inst_mem_interface_1_to_inst_mem;
  wire [10:0] instructiondecode_1_opcode, instructiondecode_1_opcodealu, PR2ALUCt_Rt_opcode_out;
  wire [31:0] adder_1_out, ALU_result, branchaddress_1_branchaddress, data_mem_interface_1_data_from_mem,
       data_mem_interface_1_data_from_memory, inst_mem_interface_1_instruction,
       instructiondecode_1_sign_ext_0_31, multiplexer_2_out, multiplexer_3_out, multiplexer_4_out, PC_q,
       pipereg3br_1_br_out, pipereg3dp_1_alu_result_out, pipereg3dp_1_rt_out, pipereg4dp_1_alu_out,
       pipereg4dp_1_memory_out, PR1_ir_out, PR1_pc_4_out, PR2DP_a_reg, PR2DP_b_reg, PR2DP_sign_ext_2,
       PR2PC_pc_4_out, ram_1_data, Register_file_readdata1, Register_file_readdata2, signextend_1_out_2;

  Register #(.width(32)) PC (.D(multiplexer_3_out), .Q(PC_q), .clk(Clock_out), .clr(Reset));  // open: en
  Clock Clock (.out(Clock_out));
  Adder #(.width(32)) adder_1 (.a(32'h4), .b(PC_q), .out(adder_1_out));  // open: cin, cout
  Inst_Mem_Interface inst_mem_interface_1 (
    .Instruction_Address(PC_q), .To_Inst_Mem(inst_mem_interface_1_to_inst_mem),
    .Mem_To_Interface(ram_1_data), .Instruction(inst_mem_interface_1_instruction));
  PipeReg1 PR1 (
    .PC_4(adder_1_out), .Instruction(inst_mem_interface_1_instruction), .Clock(Clock_out), .Reset(Reset),
    .PC_4_out(PR1_pc_4_out), .IR_out(PR1_ir_out));
  InstructionDecode instructiondecode_1 (
    .Instruction(PR1_ir_out), .opcode(instructiondecode_1_opcode), .rn(instructiondecode_1_rn),
    .rm(instructiondecode_1_rm), .rd_rt(instructiondecode_1_rd_rt),
    .Sign_Ext_0_31(instructiondecode_1_sign_ext_0_31), .opcodeALU(instructiondecode_1_opcodealu));  // open: shamt
  RAM #(.dataWidth(32)) ram_1 (
    .addr(inst_mem_interface_1_to_inst_mem), .data(ram_1_data), .sel(1'b1), .clk(1'b0), .ld(1'b1),
    .clr(Clear_Instr_Mem));
  Control Control (
    .op(instructiondecode_1_opcode), .Unconditional_Branch(Control_unconditional_branch),
    .Conditional_Branch(Control_conditional_branch), .MemToReg(Control_memtoreg), .MemRead(Control_memread),
    .MemWrite(Control_memwrite), .ALUsrc(Control_alusrc), .ALUop(Control_aluop), .RegWrite(Control_regwrite),
    .Reg2Loc(Control_reg2loc));
  Registers Register_file (
    .ReadRegister1(instructiondecode_1_rn), .ReadRegister2(multiplexer_1_out),
    .WriteRegister(pipereg3_4reg_2_destination_reg_2), .WriteData(multiplexer_4_out),
    .Write(pipereg4crtl_1_regwrite_out), .Clock(Clock_out), .Clear(Reset),
    .ReadData1(Register_file_readdata1), .ReadData2(Register_file_readdata2));
  Multiplexer #(.width(5), .enable("false")) multiplexer_1 (
    .in0(instructiondecode_1_rm), .in1(instructiondecode_1_rd_rt), .out(multiplexer_1_out),
    .sel(Control_reg2loc));
  SignExtend signextend_1 (._0_31(instructiondecode_1_sign_ext_0_31), .out_2(signextend_1_out_2));
  PipeReg2PC PR2PC (.PC_4_in(PR1_pc_4_out), .Clock(Clock_out), .Reset(Reset), .PC_4_out(PR2PC_pc_4_out));
  PipeReg2Ctrl PR2Ctr (
    .Unconditional_Branch(Control_unconditional_branch), .Conditional_Branch(Control_conditional_branch),
    .MemToReg(Control_memtoreg), .MemRead(Control_memread), .MemWrite(Control_memwrite),
    .ALUsrc(Control_alusrc), .ALUOp(Control_aluop), .RegWrite(Control_regwrite), .Clock(Clock_out),
    .Reset(Reset), .Uncond_Branch_out(PR2Ctr_uncond_branch_out), .Cond_Branch_out(PR2Ctr_cond_branch_out),
    .MemToReg_out(PR2Ctr_memtoreg_out), .MemRead_out(PR2Ctr_memread_out), .MemWrite_2(PR2Ctr_memwrite_2),
    .ALUsrc_out(PR2Ctr_alusrc_out), .ALUOp_out(PR2Ctr_aluop_out), .RegWrite_out(PR2Ctr_regwrite_out));
  PipeReg2DP PR2DP (
    .A_Register(Register_file_readdata1), .B_Register(Register_file_readdata2),
    .Sign_Ext(signextend_1_out_2), .Clock(Clock_out), .Reset(Reset), .A_Reg(PR2DP_a_reg),
    .B_Reg(PR2DP_b_reg), .Sign_Ext_2(PR2DP_sign_ext_2));
  PipeReg2ALUCtrRt PR2ALUCt_Rt (
    .OpCode(instructiondecode_1_opcodealu), .Rt(instructiondecode_1_rd_rt), .Clock(Clock_out), .Reset(Reset),
    .OpCode_out(PR2ALUCt_Rt_opcode_out), .Rt_out(PR2ALUCt_Rt_rt_out));
  BranchAddress branchaddress_1 (
    .PC_4(PR2PC_pc_4_out), .Address(PR2DP_sign_ext_2), .BranchAddress(branchaddress_1_branchaddress));
  ALU ALU (
    .A(PR2DP_a_reg), .B(multiplexer_2_out), .Operation(ALU_Control_operation), .Zero(ALU_zero),
    .Result(ALU_result));  // open: Sign, Overflow, Carry_Out
  Multiplexer #(.width(32), .enable("false")) multiplexer_2 (
    .in0(PR2DP_b_reg), .in1(PR2DP_sign_ext_2), .out(multiplexer_2_out), .sel(PR2Ctr_alusrc_out));
  ALUcontrol ALU_Control (.ALUop(PR2Ctr_aluop_out), .opcode(PR2ALUCt_Rt_opcode_out), .Operation(ALU_Control_operation));
  PipeReg3Br pipereg3br_1 (
    .BR_In(branchaddress_1_branchaddress), .Clock(Clock_out), .Reset(Reset), .BR_Out(pipereg3br_1_br_out));
  PipeReg3Ctrl pipereg3ctrl_1 (
    .Unconditional_Branch(PR2Ctr_uncond_branch_out), .Conditional_Branch(PR2Ctr_cond_branch_out),
    .MemToReg(PR2Ctr_memtoreg_out), .MemRead(PR2Ctr_memread_out), .MemWrite(PR2Ctr_memwrite_2),
    .RegWrite(PR2Ctr_regwrite_out), .Clock(Clock_out), .Reset(Reset),
    .Uncond_Branch_out(pipereg3ctrl_1_uncond_branch_out), .Cond_Branch_out(pipereg3ctrl_1_cond_branch_out),
    .MemToReg_out(pipereg3ctrl_1_memtoreg_out), .MemRead_out(pipereg3ctrl_1_memread_out),
    .MemWrite_2(pipereg3ctrl_1_memwrite_2), .RegWrite_out(pipereg3ctrl_1_regwrite_out));
  PipeReg3DP pipereg3dp_1 (
    .ALU_Zero_In(ALU_zero), .ALU_result_in(ALU_result), .rt_in(PR2DP_b_reg), .Clock(Clock_out),
    .Reset(Reset), .ALU_Zero_Out(pipereg3dp_1_alu_zero_out), .ALU_result_out(pipereg3dp_1_alu_result_out),
    .rt_out(pipereg3dp_1_rt_out));
  PipeReg3_4Reg pipereg3_4reg_1 (
    .Destination_reg(PR2ALUCt_Rt_rt_out), .Clock(Clock_out), .Reset(Reset),
    .Destination_reg_2(pipereg3_4reg_1_destination_reg_2));
  BranchControl branchcontrol_1 (
    .UnconditionalBranch(pipereg3ctrl_1_uncond_branch_out),
    .ConditionalBranch__CBZ(pipereg3ctrl_1_cond_branch_out), .Zero(pipereg3dp_1_alu_zero_out),
    .control(branchcontrol_1_control));
  Multiplexer #(.width(32), .enable("false")) multiplexer_3 (
    .in0(adder_1_out), .in1(pipereg3br_1_br_out), .out(multiplexer_3_out), .sel(branchcontrol_1_control));
  PipeReg4Crtl pipereg4crtl_1 (
    .MemToReg_in(pipereg3ctrl_1_memtoreg_out), .RegWrite_in(pipereg3ctrl_1_regwrite_out), .Clock(Clock_out),
    .Reset(Reset), .MemToReg_out(pipereg4crtl_1_memtoreg_out), .RegWrite_out(pipereg4crtl_1_regwrite_out));
  PipeReg4DP pipereg4dp_1 (
    .ALU_in(pipereg3dp_1_alu_result_out), .Memory_in(data_mem_interface_1_data_from_memory),
    .Clock(Clock_out), .Reset(Reset), .ALU_out(pipereg4dp_1_alu_out), .Memory_out(pipereg4dp_1_memory_out));
  Data_Mem_Interface data_mem_interface_1 (
    .Data_Address(pipereg3dp_1_alu_result_out), .Data_to_Memory(pipereg3dp_1_rt_out),
    .MemWrite(pipereg3ctrl_1_memwrite_2), .MemRead(pipereg3ctrl_1_memread_out),
    .Clock___Rising_Edge(Clock_out), .Address_To_Mem(data_mem_interface_1_address_to_mem),
    .Mem_Control(data_mem_interface_1_mem_control), .Data_To_Mem(data_mem_interface_1_data_from_mem),
    .Data_From_Mem(data_mem_interface_1_data_from_mem),
    .Data_from_Memory(data_mem_interface_1_data_from_memory));
  PipeReg3_4Reg pipereg3_4reg_2 (
    .Destination_reg(pipereg3_4reg_1_destination_reg_2), .Clock(Clock_out), .Reset(Reset),
    .Destination_reg_2(pipereg3_4reg_2_destination_reg_2));
  RAM #(.dataWidth(32)) ram_2 (
    .addr(data_mem_interface_1_address_to_mem), .data(data_mem_interface_1_data_from_mem), .sel(1'b1),
    .clk(data_mem_interface_1_mem_control[0]), .ld(data_mem_interface_1_mem_control[1]), .clr(Clear_Data_Mem));
  Multiplexer #(.width(32), .enable("false")) multiplexer_4 (
    .in0(pipereg4dp_1_alu_out), .in1(pipereg4dp_1_memory_out), .out(multiplexer_4_out),
    .sel(pipereg4crtl_1_memtoreg_out));

  // Notes on the sheet:
  //   Caio Brighenti 
  //   11/29/2017
  //   Decode
  //   Extend
  //   EX/Mem
  //   Mem/WB
endmodule
