// Logisim project control.circ as structural Verilog: 7 circuits, main circuit ALUcontrol_0
module ALUcontrol_0 (
  input  ALUop_1,
  input  ALUop_0,
  input  op_21,
  input  op_22,
  input  op_23,
  input  op_24,
  input  op_25,
  input  op_26,
  input  op_27,
  input  op_28,
  input  op_29,
  input  op_30,
  input  op_31,
  output Operation_0,
  output Operation_1,
  output Operation_2,
  output Operation_3
);

  wire and_2_out, not_1_out, not_2_out, not_3_out;

  not not_1 (not_1_out, op_29);
  not not_2 (not_2_out, op_30);
  not not_3 (not_3_out, op_24);
  and and_1 (Operation_0, op_29, not_2_out, op_31);
  not not_4 (Operation_1, and_2_out);
  and and_2 (and_2_out, op_25, not_3_out);
  and and_3 (Operation_2, not_1_out, op_30);

  assign Operation_3 = 1'b0;
endmodule

module Control_0 (
  input  op_21,
  input  op_22,
  input  op_23,
  input  op_24,
  input  op_25,
  input  op_26,
  input  op_27,
  input  op_28,
  input  op_29,
  input  op_30,
  input  op_31,
  output UnconditionalBranch,
  output ConditionalBranch,
  output MemToReg,
  output MemRead,
  output MemWrite,
  output ALUsrc,
  output RegWrite,
  output Reg2Loc
);

  wire and_2_out, and_3_out, and_4_out, and_5_out, and_6_out, and_7_out, and_8_out, and_9_out, and_10_out,
       and_11_out, and_12_out, and_13_out, and_14_out, and_15_out, and_16_out, and_17_out, and_18_out,
       and_19_out, and_20_out, and_21_out, and_23_out, and_24_out, and_25_out, and_26_out, and_27_out,
       and_28_out, and_29_out, and_30_out, and_31_out, and_32_out, and_33_out, and_34_out, and_35_out,
       and_36_out, and_37_out, and_38_out, and_39_out, and_40_out, and_41_out, and_42_out, and_43_out,
       and_44_out, nand_1_out, nand_2_out, not_1_out, not_2_out, not_3_out, not_4_out, not_5_out, not_6_out,
       not_7_out, not_8_out, not_9_out, not_10_out, not_11_out, not_12_out, not_13_out, not_14_out,
       not_15_out, not_16_out, not_17_out, not_18_out, not_19_out, not_20_out, not_21_out, not_22_out,
       not_23_out, not_24_out, not_25_out, not_26_out, not_27_out, not_28_out, not_29_out, not_30_out,
       not_31_out, not_32_out, not_33_out, not_34_out, not_35_out, not_36_out, not_37_out, not_38_out,
       not_39_out, not_40_out, not_41_out, not_42_out, not_43_out, not_44_out, not_45_out, not_46_out,
       not_47_out, not_48_out, not_49_out, not_50_out, not_51_out, not_52_out, not_53_out, not_54_out,
       not_55_out, not_56_out, not_57_out, not_58_out, not_59_out, not_60_out, not_61_out, not_62_out,
       not_63_out, not_64_out, not_65_out, not_66_out, not_67_out, not_68_out, not_69_out, not_70_out,
       not_71_out, not_72_out;

  not not_1 (not_1_out, op_31);
  not not_2 (not_2_out, op_30);
  not not_3 (not_3_out, op_29);
  not not_4 (not_4_out, op_27);
  not not_5 (not_5_out, op_27);
  not not_6 (not_6_out, op_27);
  not not_7 (not_7_out, op_27);
  not not_8 (not_8_out, op_26);
  not not_9 (not_9_out, op_27);
  not not_10 (not_10_out, op_27);
  not not_11 (not_11_out, op_28);
  not not_12 (not_12_out, op_26);
  not not_13 (not_13_out, op_27);
  not not_14 (not_14_out, op_26);
  not not_15 (not_15_out, op_27);
  not not_16 (not_16_out, op_26);
  not not_17 (not_17_out, op_27);
  not not_18 (not_18_out, op_26);
  not not_19 (not_19_out, op_27);
  not not_20 (not_20_out, op_26);
  not not_21 (not_21_out, op_27);
  not not_22 (not_22_out, op_25);
  not not_23 (not_23_out, op_25);
  not not_24 (not_24_out, op_25);
  not not_25 (not_25_out, op_25);
  not not_26 (not_26_out, op_25);
  not not_27 (not_27_out, op_25);
  not not_28 (not_28_out, op_25);
  not not_29 (not_29_out, op_25);
  not not_30 (not_30_out, op_25);
  not not_31 (not_31_out, op_25);
  not not_32 (not_32_out, op_31);
  not not_33 (not_33_out, op_30);
  not not_34 (not_34_out, op_29);
  not not_35 (not_35_out, op_27);
  not not_36 (not_36_out, op_31);
  not not_37 (not_37_out, op_30);
  not not_38 (not_38_out, op_29);
  not not_39 (not_39_out, op_27);
  not not_40 (not_40_out, op_24);
  not not_41 (not_41_out, op_26);
  not not_42 (not_42_out, op_27);
  not not_43 (not_43_out, op_26);
  not not_44 (not_44_out, op_27);
  not not_45 (not_45_out, op_26);
  not not_46 (not_46_out, op_27);
  not not_47 (not_47_out, op_26);
  not not_48 (not_48_out, op_29);
  not not_49 (not_49_out, op_26);
  not not_50 (not_50_out, op_30);
  not not_51 (not_51_out, op_26);
  not not_52 (not_52_out, op_31);
  not not_53 (not_53_out, op_26);
  not not_54 (not_54_out, op_28);
  not not_55 (not_55_out, op_26);
  not not_56 (not_56_out, op_26);
  not not_57 (not_57_out, op_26);
  not not_58 (not_58_out, op_26);
  not not_59 (not_59_out, op_26);
  not not_60 (not_60_out, op_25);
  not not_61 (not_61_out, op_25);
  not not_62 (not_62_out, op_25);
  not not_63 (not_63_out, op_25);
  not not_64 (not_64_out, op_25);
  not not_65 (not_65_out, op_25);
  not not_66 (not_66_out, op_25);
  not not_67 (not_67_out, op_25);
  not not_68 (not_68_out, op_25);
  not not_69 (not_69_out, op_25);
  and and_1 (UnconditionalBranch, not_1_out, not_2_out, not_3_out, op_28, not_4_out, op_26);
  and and_2 (and_2_out, not_5_out, op_31);
  and and_3 (and_3_out, not_6_out, op_30);
  and and_4 (and_4_out, not_7_out, op_29);
  and and_5 (and_5_out, not_8_out, not_9_out, op_28);
  and and_6 (and_6_out, op_26, not_10_out, not_11_out);
  and and_7 (and_7_out, op_25, not_12_out, not_13_out);
  and and_8 (and_8_out, op_24, not_14_out, not_15_out);
  and and_9 (and_9_out, op_23, not_16_out, not_17_out);
  and and_10 (and_10_out, op_22, not_18_out, not_19_out);
  and and_11 (and_11_out, op_21, not_20_out, not_21_out);
  and and_12 (and_12_out, not_22_out, op_31);
  and and_13 (and_13_out, not_23_out, op_30);
  and and_14 (and_14_out, not_24_out, op_29);
  and and_15 (and_15_out, not_25_out, op_28);
  and and_16 (and_16_out, not_26_out, op_27);
  and and_17 (and_17_out, not_27_out, op_26);
  and and_18 (and_18_out, op_24, not_28_out);
  and and_19 (and_19_out, op_23, not_29_out);
  and and_20 (and_20_out, op_22, not_30_out);
  and and_21 (and_21_out, op_21, not_31_out);
  and and_22 (ALUsrc, not_40_out, op_30);
  and and_23 (and_23_out, not_41_out, not_42_out, op_31);
  and and_24 (and_24_out, not_43_out, not_44_out, op_30);
  and and_25 (and_25_out, not_45_out, not_46_out, op_29);
  and and_26 (and_26_out, not_47_out, op_28, not_48_out);
  and and_27 (and_27_out, not_49_out, op_28, not_50_out);
  and and_28 (and_28_out, not_51_out, op_28, not_52_out);
  and and_29 (and_29_out, not_53_out, op_27, not_54_out);
  and and_30 (and_30_out, op_25, not_55_out);
  and and_31 (and_31_out, op_24, not_56_out);
  and and_32 (and_32_out, op_23, not_57_out);
  and and_33 (and_33_out, op_22, not_58_out);
  and and_34 (and_34_out, op_21, not_59_out);
  and and_35 (and_35_out, not_60_out, op_31);
  and and_36 (and_36_out, not_61_out, op_30);
  and and_37 (and_37_out, not_62_out, op_29);
  and and_38 (and_38_out, not_63_out, op_28);
  and and_39 (and_39_out, not_64_out, op_27);
  and and_40 (and_40_out, not_65_out, op_26);
  and and_41 (and_41_out, op_24, not_66_out);
  and and_42 (and_42_out, op_23, not_67_out);
  and and_43 (and_43_out, op_22, not_68_out);
  and and_44 (and_44_out, op_21, not_69_out);
  nand nand_1 (nand_1_out, not_32_out, not_33_out, not_34_out, op_28, not_35_out, op_26);
  and and_45 (MemRead, nand_1_out, op_22, not_70_out);
  not not_70 (not_70_out, op_26);
  nand nand_2 (nand_2_out, not_36_out, not_37_out, not_38_out, op_28, not_39_out, op_26);
  not not_71 (not_71_out, op_22);
  not not_72 (not_72_out, op_24);
  or or_1 (ConditionalBranch, and_2_out, and_3_out, and_4_out, and_5_out, and_6_out, and_7_out, and_8_out, and_9_out, and_10_out, and_11_out);
  or or_2 (MemToReg, and_12_out, and_13_out, and_14_out, and_15_out, and_16_out, and_17_out, and_18_out, and_19_out, and_20_out, and_21_out);
  and and_46 (MemWrite, nand_2_out, not_71_out, not_72_out, op_30);
  or or_3 (RegWrite, and_23_out, and_24_out, and_25_out, and_26_out, and_27_out, and_28_out, and_29_out, and_30_out, and_31_out, and_32_out, and_33_out, and_34_out);
  or or_4 (Reg2Loc, and_35_out, and_36_out, and_37_out, and_38_out, and_39_out, and_40_out, and_41_out, and_42_out, and_43_out, and_44_out);
endmodule

module Control_1 (
  input  op_21,
  input  op_22,
  input  op_23,
  input  op_24,
  input  op_25,
  input  op_26,
  input  op_27,
  input  op_28,
  input  op_29,
  input  op_30,
  input  op_31,
  output ALUop_1,
  output ALUop_0
);

  wire and_1_out, and_2_out, not_2_out, not_3_out, not_4_out;

  not not_1 (ALUop_1, op_28);
  not not_2 (not_2_out, op_23);
  not not_3 (not_3_out, op_27);
  not not_4 (not_4_out, op_30);
  and and_1 (and_1_out, not_2_out, not_3_out);
  and and_2 (and_2_out, op_22, not_4_out);
  or or_1 (ALUop_0, and_1_out, and_2_out, op_21);
endmodule

module Fake_Control (
  input  [9:0] test,
  input  [10:0] op,
  output Branch,
  output Conditional_Branch,
  output MemToReg,
  output MemRead,
  output MemWrite,
  output ALUsrc,
  output [1:0] ALUop,
  output RegWrite,
  output Reg2Loc
);


  assign ALUop = test[3:2];
  assign ALUsrc = test[4];
  assign Branch = test[9];
  assign Conditional_Branch = test[8];
  assign MemRead = test[6];
  assign MemToReg = test[7];
  assign MemWrite = test[5];
  assign Reg2Loc = test[0];
  assign RegWrite = test[1];
endmodule

module Fake_ALUcontrol (
  input  [3:0] test,
  input  [1:0] ALUop,
  input  [10:0] opcode,
  output [3:0] Operation
);


  assign Operation = test;
endmodule

module Control (
  input  [10:0] op,
  output Unconditional_Branch,
  output Conditional_Branch,
  output MemToReg,
  output MemRead,
  output MemWrite,
  output ALUsrc,
  output [1:0] ALUop,
  output RegWrite,
  output Reg2Loc
);

  Control_0 control_0_1 (
    .op_21(op[0]), .op_22(op[1]), .op_23(op[2]), .op_24(op[3]), .op_25(op[4]), .op_26(op[5]), .op_27(op[6]),
    .op_28(op[7]), .op_29(op[8]), .op_30(op[9]), .op_31(op[10]), .UnconditionalBranch(Unconditional_Branch),
    .ConditionalBranch(Conditional_Branch), .MemToReg(MemToReg), .MemRead(MemRead), .MemWrite(MemWrite),
    .ALUsrc(ALUsrc), .RegWrite(RegWrite), .Reg2Loc(Reg2Loc));
  Control_1 control_1_1 (
    .op_21(op[0]), .op_22(op[1]), .op_23(op[2]), .op_24(op[3]), .op_25(op[4]), .op_26(op[5]), .op_27(op[6]),
    .op_28(op[7]), .op_29(op[8]), .op_30(op[9]), .op_31(op[10]), .ALUop_1(ALUop[1]), .ALUop_0(ALUop[0]));
endmodule

module ALUcontrol (
  input  [1:0] ALUop,
  input  [10:0] opcode,
  output [3:0] Operation
);

  ALUcontrol_0 alucontrol_0_1 (
    .ALUop_1(ALUop[1]), .ALUop_0(ALUop[0]), .op_21(opcode[0]), .op_22(opcode[1]), .op_23(opcode[2]),
    .op_24(opcode[3]), .op_25(opcode[4]), .op_26(opcode[5]), .op_27(opcode[6]), .op_28(opcode[7]),
    .op_29(opcode[8]), .op_30(opcode[9]), .op_31(opcode[10]), .Operation_0(Operation[0]),
    .Operation_1(Operation[1]), .Operation_2(Operation[2]), .Operation_3(Operation[3]));
endmodule
